// Logisim project example.circ as structural Verilog: 1 circuit, main circuit main
module main (
  input  reset
);

  wire and_2_out, and_3_out, clock_1_out, d_ff_1_qn, Keyboard_1_avail, s_r_ff_1_q, shift_register_1_p2,
       shift_register_1_p7, t_ff_1_q, Timer_1_p5, Video_8_Color_RGB_32x32_1_p3;
  wire [6:0] Keyboard_1_data;
  wire [10:0] counter_1_q, Video_8_Color_RGB_32x32_1_p4;
  wire [23:0] multiplexer_1_out, multiplexer_2_out, Video_8_Color_RGB_32x32_1_p6;

  Clock clock_1 (.out(clock_1_out));
  Keyboard Keyboard_1 (
    .clk(clock_1_out), .re(and_3_out), .clr(reset), .avail(Keyboard_1_avail), .data(Keyboard_1_data));
  // Shift_Register shift_register_1: pin names not known; wires that end beside it: reset, shift_register_1_p2, 1'b1, clock_1_out, 1'b0, 1'b0, shift_register_1_p7
  and and_1 (shift_register_1_p2, Keyboard_1_avail, ~s_r_ff_1_q);  // AND_Gate
  D_Flip_Flop d_ff_1 (.D(1'b1), .clk(clock_1_out), .Qn(d_ff_1_qn), .reset(reset));  // open: Q, preset
  S_R_Flip_Flop s_r_ff_1 (
    .S(and_2_out), .R(and_3_out), .clk(clock_1_out), .Q(s_r_ff_1_q), .reset(reset));  // open: Qn, preset
  and and_2 (and_2_out, Keyboard_1_avail, ~and_3_out);  // AND_Gate
  Counter #(.max('h7ff), .width(11)) counter_1 (
    .clr(reset), .load(1'b0), .up(1'b1), .count(s_r_ff_1_q), .clk(clock_1_out), .Q(counter_1_q));  // open: D, carry
  // Timer Timer_1: pin names not known; wires that end beside it: 16'h3e8, d_ff_1_qn, clock_1_out, reset, Timer_1_p5
  T_Flip_Flop t_ff_1 (.T(Timer_1_p5), .clk(clock_1_out), .Q(t_ff_1_q), .reset(reset));  // open: Qn, preset
  Multiplexer #(.width(24)) multiplexer_1 (
    .in0(24'h7f7f7f), .in1({24{1'b1}}), .out(multiplexer_1_out), .sel(shift_register_1_p7));
  and and_3 (and_3_out, counter_1_q[0], counter_1_q[1], counter_1_q[2]);
  Multiplexer #(.width(24)) multiplexer_2 (.in0(24'hff0000), .in1(24'hff00), .out(multiplexer_2_out), .sel(t_ff_1_q));
  // RGB_Video #(.cursor("No Cursor"), .width(64)) Video_8_Color_RGB_32x32_1: pin names not known; wires that end beside it: reset, clock_1_out, Video_8_Color_RGB_32x32_1_p3, Video_8_Color_RGB_32x32_1_p4[5:0], Video_8_Color_RGB_32x32_1_p4[10:6], Video_8_Color_RGB_32x32_1_p6
  or or_1 (Video_8_Color_RGB_32x32_1_p3, s_r_ff_1_q, Timer_1_p5);
  Multiplexer #(.width(24)) multiplexer_3 (
    .in0(multiplexer_1_out), .in1(multiplexer_2_out), .out(Video_8_Color_RGB_32x32_1_p6), .sel(Timer_1_p5));
  Multiplexer #(.width(11)) multiplexer_4 (
    .in0(counter_1_q), .in1(11'h7df), .out(Video_8_Color_RGB_32x32_1_p4), .sel(Timer_1_p5));
endmodule
